// Digital circuit project06.dig as structural Verilog
module project06 (
  input  CLK,
  input  EN,
  input  CLR,
  input  [4:0] PROG,
  output [63:0] A0,
  output [63:0] A1,
  output [63:0] A2,
  output DONE
);

  wire ALUSrcA, and_2_out, CLK_t, load, MR, PCBr, PCsel, RFW, store, WDsel;
  wire [1:0] sz;
  wire [2:0] ALUSrcB, BROp;
  wire [3:0] ALUOp;
  wire [4:0] rd, rs1, rs2;
  wire [31:0] iw;
  wire [63:0] alu_1_r, imm_I, immdecoder_1_imm_b, immdecoder_1_imm_j, immdecoder_1_imm_s, immdecoder_1_imm_u,
       immdecoder_1_shift, loads_read_dout, multiplexer_1_out, multiplexer_2_out, multiplexer_3_out,
       multiplexer_4_out, multiplexer_5_out, PC, PC_plus_4, ramdualport_1_d, register_file_1_rd0,
       register_file_1_rd1, stores_write_dout, x0, x1, x2, x3, x4, x5, x6, x7, x8, x9, x13, x14, x15, x16,
       x17, x18, x19, x20, x21, x22, x23, x24, x25, x26, x27, x28, x29, x30, x31;

  Multiplexer #(.Bits(64)) multiplexer_1 (
    .sel(PCBr), .in_0(PC_plus_4), .in_1(multiplexer_5_out), .out(multiplexer_1_out));
  // Probe on PC
  // Probe on iw
  // Probe on rs1
  // Probe on rs2
  // Probe on rd
  // Probe on imm_I
  _64_bit_register _64_bit_register_1 (.D(multiplexer_1_out), .CLR(CLR), .EN(EN), .CLK(CLK_t), .Q(PC));
  and and_1 (CLK_t, CLK, ~DONE);  // And
  Comparator #(.Bits(32)) END (.a(iw), .b(32'hc0001073), .eq(DONE));  // open: gt, lt
  LED led_1 (.in(DONE));
  // Probe on x0
  // Probe on x1
  // Probe on x2
  // Probe on x3
  // Probe on x4
  // Probe on x5
  // Probe on x6
  // Probe on x7
  // inst_mem inst_mem_1: pin names not known; wires that end beside it: PROG, PC[9:2], iw
  Add #(.Bits(64)) u_PC_plus_4 (.a(PC), .b(64'h4), .c_i(1'b0), .s(PC_plus_4));  // open: c_o
  // Probe on x8
  // Probe on x9
  // Probe on A0
  // Probe on A1
  // Probe on A2
  // Probe on x13
  // Probe on x14
  // Probe on x15
  InstDecoder2 instdecoder2_1 (
    .IW(iw), .load(load), .store(store), .MR(MR), .size(sz), .BROp(BROp), .WDsel(WDsel), .PCsel(PCsel),
    .ALUSrcB(ALUSrcB), .ALUSrcA(ALUSrcA), .ALUOp(ALUOp), .RFW(RFW));
  RegDecoder regdecoder_1 (.IW(iw), .RS1(rs1), .RS2(rs2), .RD(rd));
  ImmDecoder immdecoder_1 (
    .IW(iw), .imm_I(imm_I), .imm_S(immdecoder_1_imm_s), .imm_B(immdecoder_1_imm_b),
    .imm_U(immdecoder_1_imm_u), .imm_J(immdecoder_1_imm_j), .Shift(immdecoder_1_shift));
  // Probe on x16
  // Probe on x17
  // Probe on x18
  // Probe on x19
  // Probe on x20
  // Probe on x21
  // Probe on x22
  // Probe on x23
  Multiplexer #(.Bits(64)) multiplexer_2 (
    .sel(WDsel), .in_0(multiplexer_5_out), .in_1(PC_plus_4), .out(multiplexer_2_out));
  // Probe on load
  // Probe on store
  // Probe on MR
  // Probe on sz
  // Probe on BROp
  // Probe on WDsel
  // Probe on PCsel
  and and_2 (and_2_out, RFW, EN);
  // Probe on x24
  // Probe on x25
  // Probe on x26
  // Probe on x27
  // Probe on x28
  // Probe on x29
  // Probe on x30
  // Probe on x31
  register_file register_file_1 (
    .ReadReg0(rs1), .ReadReg1(rs2), .WriteData(multiplexer_2_out), .WriteEn(and_2_out), .WriteReg(rd),
    .CLK(CLK_t), .CLR(CLR), .RD0(register_file_1_rd0), .RD1(register_file_1_rd1), .x0(x0), .x1(x1), .x2(x2),
    .x3(x3), .x4(x4), .x5(x5), .x6(x6), .x7(x7), .x8(x8), .x9(x9), .x10(A0), .x11(A1), .x12(A2), .x13(x13),
    .x14(x14), .x15(x15), .x16(x16), .x17(x17), .x18(x18), .x19(x19), .x20(x20), .x21(x21), .x22(x22),
    .x23(x23), .x24(x24), .x25(x25), .x26(x26), .x27(x27), .x28(x28), .x29(x29), .x30(x30), .x31(x31));
  // Probe on ALUSrcB
  // Probe on ALUSrcA
  // Probe on ALUOp
  // Probe on RFW
  Multiplexer #(.Bits(64)) multiplexer_3 (
    .sel(ALUSrcA), .in_0(register_file_1_rd0), .in_1(PC), .out(multiplexer_3_out));
  Multiplexer #(.Selector_Bits(3), .Bits(64)) multiplexer_4 (
    .sel(ALUSrcB), .in_0(register_file_1_rd1), .in_1(imm_I), .in_2(immdecoder_1_imm_s),
    .in_3(immdecoder_1_imm_b), .in_4(immdecoder_1_imm_u), .in_5(immdecoder_1_imm_j),
    .in_6(immdecoder_1_shift), .in_7({64{1'b0}}), .out(multiplexer_4_out));
  bcu bcu_1 (.PCSel(PCsel), .BRop(BROp), .A(register_file_1_rd0), .B(register_file_1_rd1), .PCbr(PCBr));
  alu alu_1 (.A(multiplexer_3_out), .B(multiplexer_4_out), .ALUOp(ALUOp), .R(alu_1_r));
  Multiplexer #(.Bits(64)) multiplexer_5 (.sel(MR), .in_0(alu_1_r), .in_1(loads_read_dout), .out(multiplexer_5_out));
  write stores_write (
    .addr(alu_1_r), .bnew(register_file_1_rd1), .Dcur(ramdualport_1_d), .SZ(sz), .Dout(stores_write_dout));
  RAMDualPort #(.AddrBits(7), .Bits(64)) ramdualport_1 (
    .A(alu_1_r[9:3]), .Din(stores_write_dout), .str(store), .C(CLK_t), .ld(load), .D(ramdualport_1_d));
  read loads_read (.addr(alu_1_r), .Din(ramdualport_1_d), .sz(sz), .Dout(loads_read_dout));

  // Other names for the same wires on the sheet: x10[63:0] = A0; x11[63:0] = A1; x12[63:0] = A2
endmodule
